# Fritzing sketch Fastlamp (saved by Fritzing 0.9.3b)
circuit board: 8cm x 2.9cm
breadboards: 1

parts:
  74X245N = IC, DIP package, 20 pins [chip_label=74X245N]
  GND = female pin header, 3 pins [form="♀ (female)"]
  1000uF = Capacitor Polarized [package=cpol-radial-1000uf-25v]
  WeMos_D1_Mini1 = WeMos D1 Mini

nets:
  N1: 74X245N.pin1, 74X245N.pin10, 74X245N.pin19, GND.pin1, 1000uF.-, WeMos_D1_Mini1.G
  N2: 74X245N.pin9, GND.pin3
  N3: 74X245N.pin11, WeMos_D1_Mini1.D5
  N4: 74X245N.pin20, GND.pin2, 1000uF.+, WeMos_D1_Mini1.5V

notes:
  5v
  DI
  GND
  FastLamp
  -
  D5
  v1.0.0 - @kokuma
